// Logisim project Multiplexer.circ as structural Verilog: 1 circuit, main circuit main
module main (
  input  A,
  input  [2:0] B_C_D,
  output Y
);

  wire not_1_out, not_2_out;

  not not_1 (not_1_out, A);
  not not_2 (not_2_out, 1'b0);
  Multiplexer #(.select(3)) multiplexer_1 (
    .in0(1'b0), .in1(not_1_out), .in2(1'b0), .in3(1'b0), .in4(A), .in5(not_1_out), .in6(not_2_out),
    .in7(not_2_out), .out(Y), .sel(B_C_D));  // open: en

  // Notes on the sheet:
  //   BC + ABD’ + A’C’D using Multiplexer
endmodule
