// Logisim project Practical 7.circ as structural Verilog: 1 circuit, main circuit main
module main (
  input  S,
  input  R,
  input  D,
  input  J,
  input  K,
  input  in_6,
  output Q,
  output Q_prime,
  output Q_2,
  output Q_prime_2,
  output Q_3,
  output Q_prime_3,
  output out_13,
  output out_14
);

  wire clock_1_out, clock_2_out, clock_3_out, clock_4_out, nand_1_out, nand_2_out, nand_3_out, nand_4_out,
       nand_5_out, nand_6_out, nand_7_out, nand_8_out, not_1_out;

  Clock clock_1 (.out(clock_1_out));
  Clock clock_2 (.out(clock_2_out));
  Clock clock_3 (.out(clock_3_out));
  not not_1 (not_1_out, D);
  Clock clock_4 (.out(clock_4_out));
  nand nand_1 (nand_1_out, S, clock_1_out);
  nand nand_2 (nand_2_out, clock_1_out, R);
  nand nand_3 (nand_3_out, D, clock_2_out);
  nand nand_4 (nand_4_out, clock_2_out, not_1_out);
  nand nand_5 (nand_5_out, Q_prime_3, J, clock_3_out);
  nand nand_6 (nand_6_out, clock_3_out, K, Q_3);
  nand nand_7 (nand_7_out, out_14, in_6, clock_4_out);
  nand nand_8 (nand_8_out, clock_4_out, in_6, out_13);
  nand nand_9 (Q, nand_1_out, Q_prime);
  nand nand_10 (Q_prime, Q, nand_2_out);
  nand nand_11 (Q_2, nand_3_out, Q_prime_2);
  nand nand_12 (Q_prime_2, Q_2, nand_4_out);
  nand nand_13 (Q_3, nand_5_out, Q_prime_3);
  nand nand_14 (Q_prime_3, Q_3, nand_6_out);
  nand nand_15 (out_13, nand_7_out, out_14);
  nand nand_16 (out_14, out_13, nand_8_out);

  // Notes on the sheet:
  //   Clk
  //   Clk
  //   Clk
  //   R
  //   R*
  //   S-R Flip Flop
  //   S
  //   D Flip Flop
  //   J-K Flip Flop
  //   S*
endmodule
