// Logisim project Practical 9.circ as structural Verilog: 1 circuit, main circuit main
module main (
  input  logic_1,
  output Qa,
  output Qb,
  output Qc,
  output Qd
);

  wire and_1_out, clock_1_out, not_1_out, not_2_out, t_ff_1_qn, t_ff_2_qn, t_ff_3_qn;

  Clock clock_1 (.out(clock_1_out));
  and and_1 (and_1_out, Qd, not_1_out, not_2_out, Qa);
  T_Flip_Flop t_ff_1 (.clk(clock_1_out), .T(logic_1), .Q(Qa), .Qn(t_ff_1_qn), .reset(and_1_out));  // open: preset, en
  not not_1 (not_1_out, Qc);
  not not_2 (not_2_out, Qb);
  T_Flip_Flop t_ff_2 (.clk(t_ff_1_qn), .T(logic_1), .Q(Qb), .Qn(t_ff_2_qn), .reset(and_1_out));  // open: preset, en
  T_Flip_Flop t_ff_3 (.clk(t_ff_2_qn), .T(logic_1), .Q(Qc), .Qn(t_ff_3_qn), .reset(and_1_out));  // open: preset, en
  T_Flip_Flop t_ff_4 (.clk(t_ff_3_qn), .T(logic_1), .Q(Qd), .reset(and_1_out));  // open: Qn, preset, en

  // Notes on the sheet:
  //   clk
endmodule
