// Logisim project Practical8.circ as structural Verilog: 1 circuit, main circuit main
module main (
  output QC,
  output QB,
  output QA
);

  wire and_1_out, clock_1_out, j_k_ff_1_qn;

  Clock clock_1 (.out(clock_1_out));
  and and_1 (and_1_out, QA, QB);
  J_K_Flip_Flop j_k_ff_1 (
    .J(and_1_out), .clk(clock_1_out), .K(1'b1), .Q(QC), .Qn(j_k_ff_1_qn));  // open: preset, en, reset
  J_K_Flip_Flop j_k_ff_2 (.J(QA), .clk(clock_1_out), .K(QA), .Q(QB));  // open: Qn, preset, en, reset
  J_K_Flip_Flop j_k_ff_3 (.J(j_k_ff_1_qn), .clk(clock_1_out), .K(1'b1), .Q(QA));  // open: Qn, preset, en, reset

  // Notes on the sheet:
  //   QB.QA
  //   Mod 5 Synchronous Counter using J-K Flip Flops
endmodule
